// Logisim project lab2exercises.circ as structural Verilog: 1 circuit, main circuit main
module main (
  input  x,
  input  y,
  input  A,
  input  B,
  input  C,
  input  D,
  input  A_2,
  input  B_2,
  input  C_2,
  input  in_10,
  input  in_11,
  input  in_12,
  input  in_13,
  input  in_14,
  output F___XOR_Gate,
  output F,
  output F_2,
  output out_18
);

  wire and_1_out, and_2_out, and_3_out, and_4_out, and_5_out, and_7_out, and_8_out, and_10_out, not_1_out,
       not_2_out;

  not not_1 (not_1_out, x);
  not not_2 (not_2_out, y);
  and and_1 (and_1_out, A, B);
  and and_2 (and_2_out, C, D);
  and and_3 (and_3_out, A_2, B_2);
  and and_4 (and_4_out, not_1_out, y);
  and and_5 (and_5_out, x, not_2_out);
  and and_6 (F, and_1_out, and_2_out);
  and and_7 (and_7_out, in_10, in_11);
  and and_8 (and_8_out, in_12, in_13);
  or or_1 (F___XOR_Gate, and_4_out, and_5_out);
  and and_9 (F_2, and_3_out, C_2);
  and and_10 (and_10_out, and_7_out, and_8_out);
  and and_11 (out_18, and_10_out, in_14);

  // Notes on the sheet:
  //   Lab 1
  //   Lab 2
  //   Lab 3
  //   First Circuit
endmodule
