// Logisim project labexercises5.circ as structural Verilog: 1 circuit, main circuit LabExercises
module LabExercises (
  input  A,
  input  A_2,
  input  A_3,
  input  B,
  input  A_4,
  input  B_2,
  input  A_5,
  input  B_3,
  input  C,
  input  D,
  input  A_6,
  input  B_4,
  input  C_2,
  input  D_2,
  input  A_7,
  input  B_5,
  input  A_8,
  input  B_6,
  input  A_9,
  input  B_7,
  input  A_10,
  input  B_8,
  input  C_3,
  input  D_3,
  output F,
  output F_2,
  output F_3,
  output F_4,
  output F_5,
  output F_6,
  output F_7,
  output F_8,
  output F_9,
  output F_10
);

  wire and_1_out, and_2_out, and_3_out, and_4_out, and_5_out, nand_2_out, nand_3_out, nand_4_out, nand_5_out,
       nand_6_out, nand_7_out, nand_8_out, nand_11_out, nand_12_out, nor_1_out, nor_2_out, nor_3_out,
       not_2_out, not_3_out, not_4_out, not_5_out, not_6_out, not_7_out, not_8_out, not_9_out, or_1_out;

  not not_1 (F, A);
  nand nand_1 (F_2, A_2, A_2);
  not not_2 (not_2_out, B_6);
  not not_3 (not_3_out, A_8);
  not not_4 (not_4_out, A_10);
  not not_5 (not_5_out, C_3);
  not not_6 (not_6_out, D_3);
  not not_7 (not_7_out, B_8);
  not not_8 (not_8_out, D_3);
  nand nand_2 (nand_2_out, A_3, B);
  nand nand_3 (nand_3_out, A_4, A_4);
  nand nand_4 (nand_4_out, B_2, B_2);
  nand nand_5 (nand_5_out, A_5, B_3);
  nand nand_6 (nand_6_out, C, D);
  nor nor_1 (nor_1_out, A_6, B_4);
  nor nor_2 (nor_2_out, C_2, D_2);
  or or_1 (or_1_out, A_7, B_5);
  and and_1 (and_1_out, A_7, B_5);
  and and_2 (and_2_out, A_8, not_2_out);
  and and_3 (and_3_out, B_6, not_3_out);
  nand nand_7 (nand_7_out, A_9, A_9);
  nand nand_8 (nand_8_out, B_7, B_7);
  nor nor_3 (nor_3_out, A_10, B_8);
  and and_4 (and_4_out, not_4_out, not_5_out, not_6_out);
  and and_5 (and_5_out, A_10, not_7_out, not_8_out);
  nand nand_9 (F_3, nand_2_out, nand_2_out);
  nand nand_10 (F_4, nand_3_out, nand_4_out);
  not not_9 (not_9_out, and_1_out);
  or or_2 (F_8, and_2_out, and_3_out);
  nand nand_11 (nand_11_out, nand_7_out, B_7);
  nand nand_12 (nand_12_out, nand_8_out, A_9);
  and and_6 (F_7, or_1_out, not_9_out);
  or or_3 (F_10, nor_3_out, and_4_out, and_5_out);
  nand nand_13 (F_5, nand_5_out, nand_6_out);
  nor nor_4 (F_6, nor_1_out, nor_2_out);
  nand nand_14 (F_9, nand_11_out, nand_12_out);

  // Notes on the sheet:
  //   Equal to each other
  //   Exercise 2
  //   Exercise 3
  //   Exercise 4
  //   Exercise 5
  //   Exercise 6
  //   Exercise 7
  //   Exercise 8
  //   Exercise 9
  //   Exercise 1
  //   Part 1
  //   Part 2
endmodule
