// Logisim project week11QuizWork.circ as structural Verilog: 1 circuit, main circuit Week11Quiz
module Week11Quiz (
  input  R,
  input  S,
  input  Not_S,
  input  Not_R,
  input  S_2,
  input  C,
  input  R_2,
  input  D,
  input  C_2,
  input  S_3,
  input  C_3,
  input  R_3,
  input  J,
  input  C_4,
  input  K,
  input  D_2,
  input  C_5,
  output Q,
  output Not_Q,
  output Q_2,
  output Not_Q_2,
  output Q_3,
  output Not_Q_3,
  output Q_4,
  output Not_Q_4,
  output Q_5,
  output Not_Q_5,
  output Q_6,
  output Not_Q_6,
  output Q_7,
  output Not_Q_7
);

  wire nand_1_out, nand_2_out, nand_5_out, nand_6_out, nand_7_out, nand_8_out, nand_9_out, nand_10_out,
       nand_11_out, nand_12_out, nand_13_out, nand_14_out, nand_17_out, nand_18_out, nand_19_out,
       nand_20_out, nand_23_out, nand_24_out, nand_25_out, nand_26_out, nand_27_out, nand_28_out, not_1_out,
       not_2_out, not_3_out, not_4_out, not_5_out;

  not not_1 (not_1_out, C_5);
  not not_2 (not_2_out, D);
  nand nand_1 (nand_1_out, S_3, C_3);
  nand nand_2 (nand_2_out, C_3, R_3);
  nor nor_1 (Q, R, Not_Q);
  nor nor_2 (Not_Q, Q, S);
  nand nand_3 (Q_2, Not_S, Not_Q_2);
  nand nand_4 (Not_Q_2, Q_2, Not_R);
  nand nand_5 (nand_5_out, S_2, C);
  nand nand_6 (nand_6_out, C, R_2);
  nand nand_7 (nand_7_out, D, C_2);
  nand nand_8 (nand_8_out, C_2, not_2_out);
  nand nand_9 (nand_9_out, Not_Q_6, J, C_4);
  nand nand_10 (nand_10_out, C_4, K, Q_6);
  nand nand_11 (nand_11_out, D_2, not_1_out);
  nand nand_12 (nand_12_out, nand_11_out, not_1_out);
  not not_3 (not_3_out, not_1_out);
  nand nand_13 (nand_13_out, nand_1_out, nand_14_out);
  nand nand_14 (nand_14_out, nand_13_out, nand_2_out);
  not not_4 (not_4_out, C_3);
  not not_5 (not_5_out, C_4);
  nand nand_15 (Q_3, nand_5_out, Not_Q_3);
  nand nand_16 (Not_Q_3, Q_3, nand_6_out);
  nand nand_17 (nand_17_out, nand_9_out, nand_18_out);
  nand nand_18 (nand_18_out, nand_17_out, nand_10_out);
  nand nand_19 (nand_19_out, nand_11_out, nand_20_out);
  nand nand_20 (nand_20_out, nand_19_out, nand_12_out);
  nand nand_21 (Q_4, nand_7_out, Not_Q_4);
  nand nand_22 (Not_Q_4, Q_4, nand_8_out);
  nand nand_23 (nand_23_out, nand_13_out, not_4_out);
  nand nand_24 (nand_24_out, not_4_out, nand_14_out);
  nand nand_25 (nand_25_out, nand_17_out, not_5_out);
  nand nand_26 (nand_26_out, not_5_out, nand_18_out);
  nand nand_27 (nand_27_out, nand_19_out, not_3_out);
  nand nand_28 (nand_28_out, nand_27_out, not_3_out);
  nand nand_29 (Q_5, nand_23_out, Not_Q_5);
  nand nand_30 (Not_Q_5, Q_5, nand_24_out);
  nand nand_31 (Q_6, nand_25_out, Not_Q_6);
  nand nand_32 (Not_Q_6, Q_6, nand_26_out);
  nand nand_33 (Q_7, nand_27_out, Not_Q_7);
  nand nand_34 (Not_Q_7, Q_7, nand_28_out);

  // Notes on the sheet:
  //   D Latch
  //   SR Latch
  //   Not S Not R Latch
  //   SR Latch with Control Input
  //   Master Slave SR Flip Flop
  //   Master Slave JK Flip Flop
  //   Master Slave D Flip Flop
  //   Y
  //   Not Y
  //   S 1 R 0 set state, S 0 R 1 reset state
  //   Same output as the control input SR latch, S 0 R 1 set state, S 1 R 0 its reset
  //   S and R are opposite of each other and they have a set and reset state.
  //   When C is 1, the set state and reset state are normal. They are controlled by the control input
  //   Reuses the input from the opposite output on the second run
  //   from each other
  //   The inputs are always opposite
  //   When C is 0, the first latch is disabled, when its 1, the second latch is disabled. SR will change the gates of the active gate
endmodule
