// Logisim project Week13Quiz.circ as structural Verilog: 1 circuit, main circuit Week13Quiz
module Week13Quiz (
  input  in_1,
  input  in_2,
  input  in_3,
  input  in_4,
  input  in_5,
  input  in_6,
  input  in_7,
  output out_8
);

  wire and_1_out, and_2_out, and_3_out, and_4_out, and_5_out, and_6_out, and_7_out, and_8_out, not_1_out,
       not_2_out, not_3_out, not_4_out, not_5_out, not_6_out, not_7_out, not_8_out, or_1_out, or_2_out,
       or_3_out, or_4_out;

  not not_1 (not_1_out, in_3);
  not not_2 (not_2_out, in_4);
  not not_3 (not_3_out, in_5);
  not not_4 (not_4_out, in_6);
  or or_1 (or_1_out, not_1_out, in_2, in_3, in_7);
  or or_2 (or_2_out, not_2_out, in_2, in_4, in_7);
  or or_3 (or_3_out, not_3_out, in_2, in_5, in_7);
  or or_4 (or_4_out, not_4_out, in_2, in_6, in_7);
  not not_5 (not_5_out, or_1_out);
  not not_6 (not_6_out, or_2_out);
  not not_7 (not_7_out, or_3_out);
  not not_8 (not_8_out, or_4_out);
  and and_1 (and_1_out, or_1_out, in_1);
  and and_2 (and_2_out, in_1, not_5_out);
  and and_3 (and_3_out, or_2_out, in_1);
  and and_4 (and_4_out, in_1, not_6_out);
  and and_5 (and_5_out, or_3_out, in_1);
  and and_6 (and_6_out, in_1, not_7_out);
  and and_7 (and_7_out, or_4_out, in_1);
  and and_8 (and_8_out, in_1, not_8_out);
  S_R_Flip_Flop s_r_ff_1 (.S(and_1_out), .R(and_2_out), .Q(out_8));  // open: clk, Qn, preset, reset, en
  S_R_Flip_Flop s_r_ff_2 (.S(and_3_out), .R(and_4_out), .Q(out_8));  // open: clk, Qn, preset, reset, en
  S_R_Flip_Flop s_r_ff_3 (.S(and_5_out), .R(and_6_out), .Q(out_8));  // open: clk, Qn, preset, reset, en
  S_R_Flip_Flop s_r_ff_4 (.S(and_7_out), .R(and_8_out), .Q(out_8));  // open: clk, Qn, preset, reset, en

  // Notes on the sheet:
  //   4x1 Ram
  //   a. F
  //   b. F
  //   c. F
  //   d. T
  //   e. T
  //   k. T
  //   f. T
  //   l. T
  //   g. T
  //   r. F
  //   m. F
  //   h. F
  //   n. F
  //   i. T
  //   o. T
  //   j. T
  //   p. T
  //   q. F
endmodule
