// Logisim project week9quiz.circ as structural Verilog: 1 circuit, main circuit Quiz 9
module Quiz_9 (
  input  b3,
  input  b2,
  input  b1,
  input  b0,
  input  in_5,
  input  in_6,
  input  in_7,
  input  in_8,
  input  in_9,
  input  in_10,
  input  in_11,
  input  in_12,
  input  in_13,
  input  in_14,
  input  in_15,
  input  O0,
  input  O1,
  input  O2,
  input  O3,
  input  O4,
  input  O5,
  input  O6,
  input  O7,
  output g3,
  output g2,
  output g1,
  output g0,
  output out_28,
  output out_29,
  output out_30,
  output out_31,
  output out_32,
  output out_33,
  output out_34,
  output out_35,
  output b0_2,
  output b1_2,
  output b2_2
);

  wire not_1_out, not_2_out, not_3_out;

  not not_1 (not_1_out, in_13);
  not not_2 (not_2_out, in_14);
  not not_3 (not_3_out, in_15);
  xor xor_1 (g2, b3, b2);
  xor xor_2 (g1, b2, b1);
  xor xor_3 (g0, b1, b0);
  _7_Segment_Display u_7_segment_display_1 (
    .g(in_8), .f(in_7), .a(in_6), .b(in_5), .e(in_9), .d(in_10), .c(in_11), .dp(in_12));
  or or_1 (b0_2, O1, O3, O5, O7);
  or or_2 (b1_2, O2, O3, O6, O7);
  or or_3 (b2_2, O4, O5, O6, O7);
  and and_1 (out_28, not_1_out, not_2_out, not_3_out);
  and and_2 (out_29, in_13, not_2_out, not_3_out);
  and and_3 (out_30, not_1_out, in_14, not_3_out);
  and and_4 (out_31, in_13, in_14, not_3_out);
  and and_5 (out_32, not_1_out, not_2_out, in_15);
  and and_6 (out_33, in_13, not_2_out, in_15);
  and and_7 (out_34, not_1_out, in_14, in_15);
  and and_8 (out_35, in_13, in_14, in_15);

  assign g3 = b3;

  // Notes on the sheet:
  //   Problem 2
  //   Problem 3
  //   Problem 1
  //   Problem 4
  //   You have 2 to the n outputs with n inputs.
  //   the main diagonal giving you 8 total outputs
  //   Each output is going to be different so you end up with a minterm in 
endmodule
