// Logisim project lab4exercises.circ as structural Verilog: 2 circuits, main circuit InLabProblems
module InLabProblems (
  input  A,
  input  B,
  input  C,
  input  A_2,
  input  B_2,
  input  C_2,
  input  A_3,
  input  B_3,
  input  C_3,
  input  A_4,
  input  B_4,
  input  C_4,
  input  A_5,
  input  B_5,
  input  B_6,
  input  A_6,
  input  A_7,
  input  B_7,
  input  C_5,
  input  A_8,
  input  B_8,
  input  C_6,
  input  A_9,
  input  A_10,
  input  A_11,
  input  A_12,
  input  A_13,
  input  B_9,
  input  A_14,
  input  B_10,
  input  A_15,
  input  B_11,
  input  A_16,
  input  B_12,
  input  A_17,
  input  B_13,
  input  A_18,
  input  B_14,
  input  A_19,
  input  B_15,
  input  A_20,
  input  B_16,
  output F,
  output F_2,
  output F_3,
  output G,
  output F_4,
  output G_2,
  output F_5,
  output G_3,
  output F_6,
  output G_4,
  output F_7,
  output F_8,
  output F_9,
  output G_5,
  output F_10,
  output G_6,
  output F_11,
  output G_7,
  output F_12,
  output G_8
);

  wire and_1_out, and_2_out, and_3_out, and_4_out, and_5_out, and_6_out, and_7_out, and_10_out, and_11_out,
       and_14_out, and_15_out, and_19_out, not_1_out, not_2_out, not_3_out, not_4_out, not_5_out, not_6_out,
       not_7_out, not_8_out, not_9_out, not_10_out, not_11_out, not_12_out, not_16_out, or_1_out, or_2_out;

  not not_1 (not_1_out, B_15);
  not not_2 (not_2_out, B);
  not not_3 (not_3_out, A_9);
  not not_4 (not_4_out, A_11);
  not not_5 (not_5_out, A_12);
  or or_1 (or_1_out, A_13, B_9);
  not not_6 (not_6_out, A_14);
  not not_7 (not_7_out, B_10);
  and and_1 (and_1_out, A_15, B_11);
  not not_8 (not_8_out, A_16);
  not not_9 (not_9_out, B_12);
  not not_10 (not_10_out, A_17);
  not not_11 (not_11_out, A_20);
  not not_12 (not_12_out, B_16);
  and and_2 (and_2_out, A, not_2_out);
  and and_3 (and_3_out, A, B);
  and and_4 (and_4_out, B, C);
  and and_5 (and_5_out, B_2, C_2);
  and and_6 (and_6_out, A_3, B_3);
  and and_7 (and_7_out, B_4, C_4);
  and and_8 (F_4, A_5, B_5);
  and and_9 (G_2, B_6, A_6);
  or or_2 (or_2_out, B_7, C_5);
  and and_10 (and_10_out, A_8, B_8);
  and and_11 (and_11_out, A_8, C_6);
  not not_13 (F_6, not_3_out);
  and and_12 (F_7, not_4_out, A_11);
  or or_3 (F_8, not_5_out, A_12);
  not not_14 (F_9, or_1_out);
  and and_13 (G_5, not_6_out, not_7_out);
  or or_4 (G_6, not_8_out, not_9_out);
  and and_14 (and_14_out, not_10_out, B_13);
  or or_5 (G_7, A_18, B_14);
  and and_15 (and_15_out, A_19, not_1_out);
  or or_6 (G_8, not_11_out, not_12_out);
  or or_7 (F_2, A_2, and_5_out);
  and and_16 (F_3, and_6_out, C_3);
  and and_17 (G, A_4, and_7_out);
  and and_18 (F_5, A_7, or_2_out);
  not not_15 (F_10, and_1_out);
  or or_8 (F_11, A_17, and_14_out);
  and and_19 (and_19_out, A_19, not_16_out);
  not not_16 (not_16_out, and_15_out);
  or or_9 (F, and_2_out, and_3_out, and_4_out);
  or or_10 (G_3, and_10_out, and_11_out);
  not not_17 (F_12, and_19_out);

  assign G_4 = A_10;

  // Notes on the sheet:
  //   Exercise 9 
  //   F Original
  //   F Simplified
  //   Exercise 1 Associative Law
  //   Exercise 2 Commutative Law
  //   Exercise 3 Distributive Law
  //   Exercise 4 Anoulment Rule
  //   Exercise 5 Rule 8
  //   Exercise 6
  //   Exercise 7 DeMorgan Theorems
  //   Exercise 8 Rule 11
  //   Problem 1
  //   First Example
  //   Second Example
  //   F Original
  //   F Simplied
  //   F = G
  //   F = G
  //   F = G
  //   F = G
  //   F = G
  //   F = 0
  //   F = 1
  //   F = G
  //   F = G
  //   F = G
endmodule

module HWProbs (
  input  A,
  input  B,
  input  C,
  input  A_2,
  input  B_2,
  input  A_3,
  input  B_3,
  input  C_2,
  input  D,
  input  A_4,
  input  B_4,
  input  C_3,
  input  A_5,
  input  B_5,
  output F,
  output F_2,
  output F_3,
  output F_4,
  output F_5
);

  wire and_1_out, and_2_out, and_3_out, and_4_out, and_5_out, not_1_out, not_2_out, not_3_out, not_4_out,
       not_5_out, not_6_out, not_7_out, not_9_out, or_1_out, or_5_out;

  not not_1 (not_1_out, A_2);
  not not_2 (not_2_out, B_2);
  not not_3 (not_3_out, D);
  not not_4 (not_4_out, A_4);
  not not_5 (not_5_out, C_3);
  and and_1 (and_1_out, A, B);
  or or_1 (or_1_out, B, C);
  or or_2 (F_2, not_1_out, not_2_out);
  and and_2 (and_2_out, A_3, B_3);
  or or_3 (F_5, A_5, B_5);
  not not_6 (not_6_out, and_2_out);
  and and_3 (and_3_out, C_2, D);
  and and_4 (and_4_out, C_2, A_3, not_3_out);
  or or_4 (F_4, not_4_out, B_4, not_5_out);
  and and_5 (and_5_out, and_1_out, or_1_out);
  or or_5 (or_5_out, not_6_out, and_3_out);
  not not_7 (not_7_out, and_4_out);
  not not_8 (F, and_5_out);
  not not_9 (not_9_out, or_5_out);
  or or_6 (F_3, not_9_out, not_7_out);

  // Notes on the sheet:
  //   Original
  //   Simplified
  //   Problem 2.2
  //   Problem 2.1
  //   Problem 2.3
  //   Original
  //   Simplified
endmodule
