// Logisim project labexercises5.circ as structural Verilog: 2 circuits, main circuit LabExercises
module LabExercises (
  input  A,
  input  A_2,
  input  A_3,
  input  B,
  input  A_4,
  input  B_2,
  input  A_5,
  input  B_3,
  input  C,
  input  D,
  input  A_6,
  input  B_4,
  input  C_2,
  input  D_2,
  input  A_7,
  input  B_5,
  input  A_8,
  input  B_6,
  input  A_9,
  input  B_7,
  input  A_10,
  input  B_8,
  input  C_3,
  input  D_3,
  input  A_11,
  input  B_9,
  input  C_4,
  input  D_4,
  output F,
  output F_2,
  output F_3,
  output F_4,
  output F_5,
  output F_6,
  output F_7,
  output F_8,
  output F_9,
  output F_10,
  output F_11
);

  wire and_1_out, and_2_out, and_3_out, and_4_out, and_5_out, and_6_out, and_7_out, and_8_out, and_9_out,
       nand_2_out, nand_3_out, nand_4_out, nand_5_out, nand_6_out, nand_7_out, nand_8_out, nand_11_out,
       nand_12_out, nor_1_out, nor_2_out, nor_3_out, not_2_out, not_3_out, not_4_out, not_5_out, not_6_out,
       not_7_out, not_8_out, not_9_out, not_10_out, or_1_out;

  not not_1 (F, A);
  nand nand_1 (F_2, A_2, A_2);
  not not_2 (not_2_out, B_6);
  not not_3 (not_3_out, A_8);
  not not_4 (not_4_out, A_10);
  not not_5 (not_5_out, C_3);
  not not_6 (not_6_out, D_3);
  not not_7 (not_7_out, B_8);
  not not_8 (not_8_out, D_3);
  not not_9 (not_9_out, A_11);
  nand nand_2 (nand_2_out, A_3, B);
  nand nand_3 (nand_3_out, A_4, A_4);
  nand nand_4 (nand_4_out, B_2, B_2);
  nand nand_5 (nand_5_out, A_5, B_3);
  nand nand_6 (nand_6_out, C, D);
  nor nor_1 (nor_1_out, A_6, B_4);
  nor nor_2 (nor_2_out, C_2, D_2);
  or or_1 (or_1_out, A_7, B_5);
  and and_1 (and_1_out, A_7, B_5);
  and and_2 (and_2_out, A_8, not_2_out);
  and and_3 (and_3_out, B_6, not_3_out);
  nand nand_7 (nand_7_out, A_9, A_9);
  nand nand_8 (nand_8_out, B_7, B_7);
  nor nor_3 (nor_3_out, A_10, B_8);
  and and_4 (and_4_out, not_4_out, not_5_out, not_6_out);
  and and_5 (and_5_out, A_10, not_7_out, not_8_out);
  nand nand_9 (F_3, nand_2_out, nand_2_out);
  nand nand_10 (F_4, nand_3_out, nand_4_out);
  not not_10 (not_10_out, and_1_out);
  or or_2 (F_8, and_2_out, and_3_out);
  nand nand_11 (nand_11_out, nand_7_out, B_7);
  nand nand_12 (nand_12_out, nand_8_out, A_9);
  and and_6 (and_6_out, A_11, C_4);
  and and_7 (and_7_out, A_11, D_4);
  and and_8 (and_8_out, B_9, not_9_out, C_4);
  and and_9 (and_9_out, not_9_out, B_9, D_4);
  and and_10 (F_7, or_1_out, not_10_out);
  or or_3 (F_10, nor_3_out, and_4_out, and_5_out);
  or or_4 (F_11, and_6_out, and_7_out, and_8_out, and_9_out);
  nand nand_13 (F_5, nand_5_out, nand_6_out);
  nor nor_4 (F_6, nor_1_out, nor_2_out);
  nand nand_14 (F_9, nand_11_out, nand_12_out);

  // Notes on the sheet:
  //   Equal to each other
  //   Exercise 2
  //   Exercise 3
  //   Exercise 4
  //   Exercise 5
  //   Exercise 6
  //   Exercise 7
  //   Exercise 8
  //   Exercise 9
  //   Exercise 1
  //   Part 1
  //   Part 2
endmodule

module HomeworkProbs (
  input  A,
  input  A_2,
  input  B,
  input  A_3,
  input  B_2,
  input  A_4,
  input  B_3,
  input  in_8,
  input  in_9,
  input  in_10,
  input  A_5,
  input  B_4,
  input  C,
  input  D,
  input  A_6,
  input  B_5,
  input  C_2,
  input  D_2,
  input  X,
  input  Y,
  input  Z,
  input  D_3,
  input  K,
  input  S,
  input  B_6,
  input  A_7,
  input  B_7,
  input  C_3,
  input  D_4,
  input  in_30,
  input  in_31,
  input  in_32,
  input  in_33,
  input  in_34,
  input  in_35,
  input  in_36,
  input  in_37,
  output F,
  output F_2,
  output F_3,
  output F_4,
  output F_5,
  output F_6,
  output F_7,
  output F_8,
  output F_9,
  output out_47,
  output out_48
);

  wire and_2_out, and_3_out, and_4_out, and_5_out, and_6_out, and_7_out, and_8_out, and_9_out, and_10_out,
       and_11_out, and_12_out, nand_1_out, nand_2_out, nand_3_out, nand_4_out, nand_5_out, nand_6_out,
       nand_7_out, nand_8_out, nand_9_out, nand_10_out, nand_11_out, nand_12_out, nand_13_out, nand_14_out,
       nand_15_out, nand_16_out, nand_17_out, nand_18_out, nor_2_out, nor_3_out, nor_4_out, nor_6_out,
       nor_7_out, nor_8_out, nor_9_out, nor_10_out, not_1_out, not_2_out, not_3_out, not_4_out, not_5_out,
       not_6_out;

  not not_1 (not_1_out, X);
  not not_2 (not_2_out, Y);
  not not_3 (not_3_out, Z);
  not not_4 (not_4_out, A_7);
  not not_5 (not_5_out, C_3);
  not not_6 (not_6_out, D_4);
  nand nand_1 (nand_1_out, in_32, in_32);
  nand nand_2 (nand_2_out, in_33, in_33);
  nor nor_1 (F, A, A);
  nor nor_2 (nor_2_out, A_2, B);
  nor nor_3 (nor_3_out, A_3, A_3);
  nor nor_4 (nor_4_out, B_2, B_2);
  and and_1 (F_4, A_4, B_3);
  nand nand_3 (nand_3_out, in_8, in_8);
  nand nand_4 (nand_4_out, in_9, in_9);
  nand nand_5 (nand_5_out, in_10, in_10);
  nand nand_6 (nand_6_out, A_5, A_5);
  and and_2 (and_2_out, D_3, K);
  and and_3 (and_3_out, K, S, B_6);
  nand nand_7 (nand_7_out, in_30, in_30);
  nor nor_5 (F_3, nor_3_out, nor_4_out);
  nand nand_8 (nand_8_out, nand_3_out, in_9);
  nand nand_9 (nand_9_out, in_8, nand_4_out);
  nand nand_10 (nand_10_out, A_6, C_2);
  nand nand_11 (nand_11_out, A_6, B_5, D_2);
  and and_4 (and_4_out, not_1_out, not_2_out, Z);
  and and_5 (and_5_out, not_1_out, Y, not_3_out);
  and and_6 (and_6_out, X, not_2_out, not_3_out);
  and and_7 (and_7_out, X, Z, Y);
  and and_8 (and_8_out, not_4_out, D_4);
  and and_9 (and_9_out, B_7, C_3);
  and and_10 (and_10_out, C_3, D_4);
  and and_11 (and_11_out, B_7, A_7);
  and and_12 (and_12_out, A_7, not_5_out, not_6_out);
  nand nand_12 (nand_12_out, nand_7_out, in_31);
  nand nand_13 (nand_13_out, in_31, in_32);
  nand nand_14 (nand_14_out, in_32, in_33);
  nand nand_15 (nand_15_out, nand_1_out, in_30, nand_2_out);
  nor nor_6 (nor_6_out, in_34, in_37);
  nor nor_7 (nor_7_out, in_35, in_36);
  nor nor_8 (nor_8_out, in_36, in_37);
  nor nor_9 (nor_9_out, in_34, in_35);
  nor nor_10 (nor_10_out, in_34, in_36, in_37);
  nor nor_11 (F_2, nor_2_out, nor_2_out);
  nand nand_16 (nand_16_out, nand_6_out, B_4, C);
  nand nand_17 (nand_17_out, nand_6_out, C, D);
  or or_1 (F_8, and_2_out, and_3_out);
  nand nand_18 (nand_18_out, in_30, in_31);
  nand nand_19 (F_6, nand_10_out, nand_11_out);
  or or_2 (F_7, and_4_out, and_5_out, and_6_out, and_7_out);
  or or_3 (F_9, and_8_out, and_9_out, and_10_out, and_11_out, and_12_out);
  nand nand_20 (out_47, nand_18_out, nand_12_out, nand_13_out, nand_14_out, nand_15_out);
  // NAND_Gate nand_21 has open pins: in0=nand_8_out, in1=nand_9_out, in2=nand_5_out, out=open
  nand nand_22 (F_5, nand_6_out, nand_16_out, nand_17_out);
  nor nor_12 (out_48, nor_6_out, nor_7_out, nor_8_out, nor_9_out, nor_10_out);

  // Notes on the sheet:
  //   Exercise 5
  //   Part C
  //   Exercise 2
  //   Exercise 3
  //   Exercise 4
  //   Exercise 7
  //   Exercise 8
  //   Exercise 9
  //   Exercise 10
  //   Part B
  //   Exercise 1
  //   Exercise 4 is equal to Exercise 3
  //   F Sop form Simplified
  //   F Pos form Simplified
endmodule
