// Logisim project lab6exercises.circ as structural Verilog: 1 circuit, main circuit HomeWorkProbs
module HomeWorkProbs (
  input  A,
  input  B,
  input  C,
  input  in_4,
  input  A_2,
  input  B_2,
  input  C_2,
  input  D,
  input  A_3,
  input  B_3,
  input  C_3,
  input  D_2,
  input  A_4,
  input  B_4,
  input  C_4,
  input  D_3,
  input  A_5,
  input  B_5,
  input  C_5,
  input  D_4,
  input  A_6,
  input  B_6,
  input  C_6,
  input  D_5,
  input  A_7,
  input  B_7,
  input  C_7,
  input  D_6,
  input  A_8,
  input  B_8,
  input  C_8,
  input  D_7,
  input  A_9,
  input  B_9,
  input  C_9,
  input  D_8,
  input  A_10,
  input  B_10,
  input  C_10,
  input  A_11,
  input  B_11,
  input  C_11,
  input  D_9,
  output F,
  output out_45,
  output F_2,
  output F_3,
  output F_4,
  output F_5,
  output F_6,
  output F_7,
  output F_8,
  output F_9,
  output F_10,
  output F_11
);

  wire and_1_out, and_2_out, and_3_out, and_4_out, and_5_out, and_6_out, and_7_out, and_8_out, and_9_out,
       and_10_out, and_11_out, and_12_out, and_13_out, and_14_out, and_15_out, and_16_out, and_17_out,
       nand_1_out, nand_2_out, nand_3_out, not_1_out, not_2_out, not_3_out, not_4_out, not_5_out, not_6_out,
       not_7_out, not_8_out, not_9_out, not_10_out, not_11_out, not_12_out, not_13_out, not_14_out,
       not_15_out, not_16_out, not_17_out, not_18_out, not_19_out, not_20_out, not_21_out, not_22_out,
       not_23_out, not_24_out, not_25_out, or_1_out, or_2_out, or_3_out, or_4_out, or_5_out, or_6_out,
       or_7_out, or_8_out, or_9_out, or_10_out, or_11_out, or_12_out, or_13_out, or_14_out, or_15_out;

  not not_1 (not_1_out, A);
  not not_2 (not_2_out, B);
  not not_3 (not_3_out, A_3);
  not not_4 (not_4_out, A_10);
  not not_5 (not_5_out, B_10);
  not not_6 (not_6_out, C_10);
  not not_7 (not_7_out, A_2);
  not not_8 (not_8_out, C_2);
  not not_9 (not_9_out, B_3);
  not not_10 (not_10_out, C_3);
  not not_11 (not_11_out, A_4);
  not not_12 (not_12_out, C_4);
  not not_13 (not_13_out, A_5);
  not not_14 (not_14_out, B_5);
  not not_15 (not_15_out, C_5);
  not not_16 (not_16_out, D_4);
  not not_17 (not_17_out, B_6);
  or or_1 (or_1_out, not_4_out, not_5_out);
  or or_2 (or_2_out, not_5_out, not_6_out);
  not not_18 (not_18_out, A_11);
  not not_19 (not_19_out, C_11);
  not not_20 (not_20_out, B_11);
  not not_21 (not_21_out, C);
  not not_22 (not_22_out, B_2);
  and and_1 (and_1_out, A_3, not_9_out);
  and and_2 (and_2_out, not_10_out, D_2);
  and and_3 (and_3_out, not_3_out, B_3);
  and and_4 (and_4_out, not_3_out, C_3);
  and and_5 (and_5_out, not_3_out, D_2);
  not not_23 (not_23_out, D_3);
  not not_24 (not_24_out, B_4);
  or or_3 (or_3_out, not_13_out, B_5, not_15_out);
  or or_4 (or_4_out, A_5, not_14_out, not_16_out);
  or or_5 (or_5_out, A_5, B_5);
  or or_6 (or_6_out, A_5, not_15_out);
  not not_25 (not_25_out, C_6);
  or or_7 (or_7_out, not_17_out, C_6, D_5);
  or or_8 (or_8_out, A_7, C_7);
  or or_9 (or_9_out, A_7, B_7, D_6);
  and and_6 (and_6_out, C_8, D_7);
  and and_7 (and_7_out, C_8, B_8);
  nand nand_1 (nand_1_out, A_9, A_9);
  nand nand_2 (nand_2_out, C_9, D_8);
  nand nand_3 (nand_3_out, B_9, C_9);
  or or_10 (or_10_out, not_18_out, D_9, not_19_out);
  or or_11 (or_11_out, not_20_out, D_9, C_11);
  and and_8 (and_8_out, A, not_2_out, C);
  and and_9 (and_9_out, not_2_out, not_21_out);
  and and_10 (and_10_out, not_1_out, C);
  and and_11 (and_11_out, not_1_out, B, not_21_out);
  and and_12 (and_12_out, B, A);
  and and_13 (and_13_out, not_7_out, B_2);
  and and_14 (and_14_out, A_2, not_22_out, not_8_out, D);
  and and_15 (and_15_out, not_22_out, C_2, D);
  and and_16 (and_16_out, not_8_out, D);
  and and_17 (and_17_out, A_2, not_8_out, D);
  or or_12 (or_12_out, not_11_out, not_12_out, D_3);
  or or_13 (or_13_out, C_4, not_23_out);
  or or_14 (or_14_out, not_12_out, not_24_out);
  or or_15 (or_15_out, A_4, not_23_out);
  and and_18 (F_10, or_1_out, or_2_out);
  and and_19 (F_6, A_6, not_25_out, or_7_out);
  and and_20 (F_7, or_8_out, or_9_out);
  or or_16 (F_8, A_8, and_6_out, and_7_out);
  nand nand_4 (F_9, nand_1_out, nand_2_out, nand_3_out);
  and and_21 (F_11, or_10_out, or_11_out);
  or or_17 (F, and_8_out, and_9_out, and_10_out, and_11_out, and_12_out);
  or or_18 (F_3, and_1_out, and_2_out, and_3_out, and_4_out, and_5_out);
  and and_22 (F_4, or_12_out, or_13_out, or_14_out, or_15_out);
  and and_23 (F_5, or_3_out, or_4_out, not_14_out, or_5_out, or_6_out);
  or or_19 (F_2, and_13_out, and_14_out, and_15_out, not_22_out, and_16_out, and_17_out);

  assign out_45 = in_4;

  // Notes on the sheet:
  //   Exercise 1 Problem 2
  //   F Simplified
  //   Exercise 1 Problem 4
  //   F Simplified
  //   Exercise 2
  //   Exercise 1 problem 1
  //   F Simplified
  //   Exercise 1 Problem 3
  //   Exercise 3
  //   Exercise 4
  //   F pos Simplified
  //   F sop Simplified
  //   Nand Configuration
  //   F is always 1 so i just kept it with nothing
  //   F Simplified
  //   F Normal
  //   F Normal
  //   F Normal
endmodule
