// Logisim project Problem1.circ as structural Verilog: 1 circuit, main circuit Week12QuizProbs
module Week12QuizProbs (
  input  A,
  input  in_2,
  input  B,
  input  Carry,
  output out_5
);

  wire and_1_out, and_2_out, clock_1_out, shift_register_1_out, xor_1_out, xor_2_out;

  xor xor_1 (xor_1_out, A, B);
  and and_1 (and_1_out, xor_1_out, Carry);
  and and_2 (and_2_out, A, B);
  xor xor_2 (xor_2_out, xor_1_out, Carry);
  or or_1 (out_5, and_1_out, and_2_out);
  Clock clock_1 (.out(clock_1_out));
  Shift_Register #(.length(1)) shift_register_1 (
    .shift(in_2), .in(xor_2_out), .clk(clock_1_out), .out(shift_register_1_out));  // open: load, clr, d0, q0
  Shift_Register #(.length(1)) shift_register_2 (
    .shift(in_2), .in(shift_register_1_out), .clk(clock_1_out));  // open: out, load, clr, d0, q0

  // Notes on the sheet:
  //   Question 1
endmodule
