// Logisim project Problem2.circ as structural Verilog: 1 circuit, main circuit main
module main (
);

  wire A_out, and_1_out, and_2_out, and_3_out, and_4_out, and_5_out, and_6_out, and_7_out, and_8_out,
       and_9_out, and_10_out, and_11_out, and_12_out, and_13_out, and_14_out, and_15_out, and_16_out,
       and_17_out, and_18_out, and_19_out, and_20_out, and_21_out, and_22_out, and_23_out, and_24_out,
       and_25_out, and_26_out, and_27_out, and_28_out, and_29_out, and_30_out, and_31_out, and_32_out,
       and_33_out, and_34_out, and_35_out, and_36_out, and_37_out, B_out, C_out, clock_1_out, D_out, E_out,
       F_out, G_out, j_k_ff_1_q, j_k_ff_1_qn, j_k_ff_2_q, j_k_ff_2_qn, j_k_ff_3_q, j_k_ff_3_qn, j_k_ff_4_q,
       not_1_out, not_2_out, not_3_out, not_4_out;

  not not_1 (not_1_out, j_k_ff_3_q);
  not not_2 (not_2_out, j_k_ff_4_q);
  J_K_Flip_Flop j_k_ff_1 (
    .J(1'b1), .clk(clock_1_out), .K(1'b1), .Q(j_k_ff_1_q), .Qn(j_k_ff_1_qn));  // open: preset, en, reset
  not not_3 (not_3_out, j_k_ff_2_q);
  J_K_Flip_Flop j_k_ff_2 (
    .J(j_k_ff_1_qn), .clk(clock_1_out), .K(j_k_ff_1_qn), .Q(j_k_ff_2_q), .Qn(j_k_ff_2_qn));  // open: preset, en, reset
  and and_1 (and_1_out, j_k_ff_2_qn, j_k_ff_1_qn);
  not not_4 (not_4_out, j_k_ff_1_q);
  Clock clock_1 (.out(clock_1_out));
  and and_2 (and_2_out, j_k_ff_3_q, j_k_ff_1_q);
  and and_3 (and_3_out, j_k_ff_4_q, j_k_ff_3_q);
  and and_4 (and_4_out, j_k_ff_4_q, j_k_ff_2_q);
  and and_5 (and_5_out, not_2_out, j_k_ff_2_q);
  and and_6 (and_6_out, j_k_ff_3_q, j_k_ff_1_q);
  and and_7 (and_7_out, j_k_ff_2_q, j_k_ff_1_q, j_k_ff_1_q);
  and and_8 (and_8_out, j_k_ff_3_q, not_3_out);
  and and_9 (and_9_out, j_k_ff_4_q, not_3_out);
  and and_10 (and_10_out, not_1_out, not_3_out);
  and and_11 (and_11_out, j_k_ff_3_q, j_k_ff_1_q);
  and and_12 (and_12_out, j_k_ff_4_q, j_k_ff_2_q, j_k_ff_1_q);
  and and_13 (and_13_out, j_k_ff_4_q, not_4_out);
  and and_14 (and_14_out, j_k_ff_2_q, not_4_out);
  and and_15 (and_15_out, j_k_ff_4_q, j_k_ff_3_q, j_k_ff_1_q);
  and and_16 (and_16_out, j_k_ff_3_q, not_3_out, not_4_out);
  and and_17 (and_17_out, not_3_out, j_k_ff_1_q);
  and and_18 (and_18_out, not_2_out, not_3_out);
  and and_19 (and_19_out, not_1_out, j_k_ff_1_q);
  and and_20 (and_20_out, not_2_out, j_k_ff_3_q);
  and and_21 (and_21_out, not_3_out, j_k_ff_1_q);
  and and_22 (and_22_out, not_2_out, j_k_ff_3_q);
  J_K_Flip_Flop j_k_ff_3 (
    .J(and_1_out), .clk(clock_1_out), .K(and_1_out), .Q(j_k_ff_3_q), .Qn(j_k_ff_3_qn));  // open: preset, en, reset
  and and_23 (and_23_out, j_k_ff_3_qn, and_1_out);
  and and_24 (and_24_out, not_2_out, j_k_ff_1_q);
  and and_25 (and_25_out, j_k_ff_4_q, not_3_out, not_4_out);
  and and_26 (and_26_out, j_k_ff_4_q, not_1_out);
  and and_27 (and_27_out, not_1_out, j_k_ff_2_q, not_4_out);
  and and_28 (and_28_out, not_2_out, not_1_out);
  and and_29 (and_29_out, not_2_out, not_3_out);
  and and_30 (and_30_out, not_2_out, not_4_out);
  and and_31 (and_31_out, j_k_ff_4_q, not_1_out, not_4_out);
  and and_32 (and_32_out, not_2_out, j_k_ff_3_q, j_k_ff_2_q);
  and and_33 (and_33_out, not_2_out, j_k_ff_2_q, not_4_out);
  and and_34 (and_34_out, not_2_out, j_k_ff_3_q);
  and and_35 (and_35_out, not_1_out, not_3_out, j_k_ff_1_q);
  and and_36 (and_36_out, j_k_ff_4_q, not_1_out, j_k_ff_2_q);
  and and_37 (and_37_out, j_k_ff_4_q, not_1_out, j_k_ff_2_q);
  J_K_Flip_Flop j_k_ff_4 (
    .J(and_23_out), .clk(clock_1_out), .K(and_23_out), .Q(j_k_ff_4_q));  // open: Qn, preset, en, reset
  or A (A_out, and_2_out, and_9_out, and_10_out, and_24_out, and_31_out, and_32_out);
  or B (B_out, and_3_out, and_11_out, and_12_out, and_25_out, and_33_out);
  or C (C_out, and_4_out, and_13_out, and_14_out, and_26_out, and_34_out);
  or D (D_out, and_5_out, and_15_out, and_16_out, and_27_out, and_35_out);
  or E (E_out, and_6_out, and_17_out, and_18_out, and_28_out);
  or F (F_out, and_7_out, and_19_out, and_20_out, and_29_out, and_36_out);
  or G (G_out, and_8_out, and_21_out, and_22_out, and_30_out, and_37_out);
  _7_Segment_Display u_7_segment_display_1 (
    .g(G_out), .f(F_out), .a(A_out), .b(B_out), .e(E_out), .d(D_out), .c(C_out));  // open: dp
  _7_Segment_Display u_7_segment_display_2 (
    .g(G_out), .f(F_out), .a(A_out), .b(B_out), .e(E_out), .d(D_out), .c(C_out));  // open: dp

  // Notes on the sheet:
  //   Question 2
endmodule
